# Fritzing sketch Basic ESP Talking Clock (saved by Fritzing 0.9.3b)
perfboards: 1

parts:
  U11 = NodeMCU V1.0
  DFPlayer_mini11 = DFPlayer mini aka FN-M16P [package="DIP (Dual Inline) [THT]"]
  SP6 = SPEAKER [package=pcb_mount_speaker]
  Bauteil1 = KY-033 Tracing Black White Line Hunting Sensor Module For Arduino
  D1 = Diode [package=diode-hv]
  J1 = female pin header, 2 pins [form="♀ (female)"]
  J3 = rounded female pin header, 3 pins [form="♀ (female rounded)"]

nets:
  N1: U11.D0, D1.A
  3V3: U11.3V3, DFPlayer_mini11.VCC, Bauteil1.V+, J3.pin3
  GND: U11.GND, DFPlayer_mini11.GND#6, Bauteil1.GND, J3.pin2
  N2: U11.D5, Bauteil1.S, J3.pin1
  N3: U11.D6, DFPlayer_mini11.RX
  N4: U11.D7, DFPlayer_mini11.TX
  N5: DFPlayer_mini11.SPK+, SP6.-, J1.pin2
  N6: DFPlayer_mini11.SPK-, SP6.+, J1.pin1
  N7: DFPlayer_mini11.Busy, D1.C

custom parts:
  NodeMCU V1.0: ESP8266 based NodeMCU
  DFPlayer mini aka FN-M16P: A Module to play Music from an SD-Card. Supports MP3 files. Built-in 3Watts Amp.
  KY-033 Tracing Black White Line Hunting Sensor Module For Arduino: Tracing Black White Line Hunting Sensor Module For Arduino Description: This is KY-033 tracking sensor. The KY-033 measures the intensity of infrared radiation and delivers it as an analog output voltage. Features: Operating voltage: 2.5 - 12V(cannot over12V) working current: 18mA-20mA at 5V Enhanced accuracy Documents: http://www.vishay.com/docs/83760/tcrt5000.pdf

// code stored in the sketch: Talking Alarm Clock.ino

