# Fritzing sketch Breadboard ESP Talking Clock with TM1637 and DS3231 (saved by Fritzing 0.9.3b)
breadboards: 1

parts:
  U11 = NodeMCU V1.0
  DFPlayer_mini11 = DFPlayer mini aka FN-M16P [package="DIP (Dual Inline) [THT]"]
  SP6 = SPEAKER [package=pcb_mount_speaker]
  ZS-042_RTC9 = ZS-042 RTC Module
  Grove1 = Grove 4 Digit Display
  Bauteil1 = KY-033 Tracing Black White Line Hunting Sensor Module For Arduino
  D1 = Diode [package=diode-hv]

nets:
  N1: U11.D0, D1.A
  N2: U11.D1, ZS-042_RTC9.SCL
  N3: U11.D2, ZS-042_RTC9.SDA
  N4: U11.D3, Grove1.CLK
  N5: U11.D4, Grove1.DIO
  VCC: U11.3V3, DFPlayer_mini11.VCC, Grove1.VCC, Bauteil1.V+
  GND: U11.GND, DFPlayer_mini11.GND#6, Grove1.GND, Bauteil1.GND
  N6: U11.D5, Bauteil1.S
  N7: DFPlayer_mini11.SPK+, SP6.-
  N8: DFPlayer_mini11.SPK-, SP6.+
  N9: DFPlayer_mini11.Busy, D1.C

custom parts:
  NodeMCU V1.0: ESP8266 based NodeMCU
  DFPlayer mini aka FN-M16P: A Module to play Music from an SD-Card. Supports MP3 files. Built-in 3Watts Amp.
  ZS-042 RTC Module: This is the ZS-042 RTC module which uses the Maxim DS3231 real time clock IC. The module has a battery holder for a LIR2032 or CR2032. The module also includes an Atmel AT24C32 32K EEPROM for storing important information. The module can operate at 3V3 and 5V.
  KY-033 Tracing Black White Line Hunting Sensor Module For Arduino: Tracing Black White Line Hunting Sensor Module For Arduino Description: This is KY-033 tracking sensor. The KY-033 measures the intensity of infrared radiation and delivers it as an analog output voltage. Features: Operating voltage: 2.5 - 12V(cannot over12V) working current: 18mA-20mA at 5V Enhanced accuracy Documents: http://www.vishay.com/docs/83760/tcrt5000.pdf

// code stored in the sketch: Talking Alarm Clock.ino

